// Digital circuit CU.dig as structural Verilog
module CU (
  input  [3:0] Opcode__IR,
  input  Zero_flag,
  input  reset,
  input  clock,
  output [2:0] ALU_Op,
  output [1:0] Read_Reg_1,
  output [1:0] Read_Reg_2,
  output [1:0] Write_Reg,
  output Write_Enabled,
  output Immediate_Load,
  output Increment,
  output Fetch_Enable
);

  wire and_2_out, and_3_out, and_4_out, and_5_out, not_2_out, not_3_out, not_4_out, not_5_out, not_6_out,
       not_7_out, not_8_out, not_9_out, not_10_out, not_11_out, not_12_out, not_13_out, not_14_out,
       not_15_out, not_16_out, not_17_out;
  wire [2:0] and_12_out, and_13_out, and_14_out, and_15_out, and_16_out, and_17_out;
  wire [2:2] and_6_out, and_7_out, and_8_out, and_9_out, and_10_out, and_11_out;
  wire [3:0] and_1_out;

  assign and_1_out = Opcode__IR & {4{clock}};  // And and_1, 4 bits wide
  not not_1 (Read_Reg_1[0], and_1_out[0]);
  not not_2 (not_2_out, and_1_out[0]);
  not not_3 (not_3_out, and_1_out[1]);
  not not_4 (not_4_out, and_1_out[1]);
  not not_5 (not_5_out, and_1_out[2]);
  not not_6 (not_6_out, and_1_out[3]);
  not not_7 (not_7_out, and_1_out[0]);
  not not_8 (not_8_out, and_1_out[0]);
  and and_2 (and_2_out, not_2_out, not_3_out, and_1_out[2]);
  and and_3 (and_3_out, not_4_out, not_5_out, not_6_out);
  or or_1 (Write_Enabled, and_1_out[0], and_1_out[2], and_1_out[3]);
  and and_4 (and_4_out, not_7_out, and_1_out[3]);
  and and_5 (and_5_out, not_8_out, and_1_out[2]);
  not not_9 (not_9_out, and_1_out[1]);
  not not_10 (not_10_out, and_1_out[2]);
  not not_11 (not_11_out, and_1_out[1]);
  not not_12 (not_12_out, and_1_out[3]);
  not not_13 (not_13_out, and_1_out[1]);
  not not_14 (not_14_out, and_1_out[2]);
  not not_15 (not_15_out, and_1_out[3]);
  not not_16 (not_16_out, and_1_out[2]);
  not not_17 (not_17_out, and_1_out[3]);
  or or_2 (Read_Reg_1[1], and_2_out, and_3_out);
  or or_3 (Immediate_Load, and_4_out, and_5_out);
  and and_6 (and_6_out[2], and_1_out[0], not_9_out, not_10_out, and_1_out[3]);
  and and_7 (and_7_out[2], and_1_out[0], not_11_out, and_1_out[2], not_12_out);
  and and_8 (and_8_out[2], and_1_out[0], not_13_out, and_1_out[2], and_1_out[3]);
  and and_9 (and_9_out[2], and_1_out[0], and_1_out[1], not_14_out, not_15_out);
  and and_10 (and_10_out[2], and_1_out[0], and_1_out[1], not_16_out, and_1_out[3]);
  and and_11 (and_11_out[2], and_1_out[0], and_1_out[1], and_1_out[2], not_17_out);
  assign and_12_out = {3{Read_Reg_1[1]}} & {3{and_6_out[2]}};  // And and_12, 3 bits wide
  assign and_13_out = {{2{Read_Reg_1[1]}}, 1'b1} & {3{and_7_out[2]}};  // And and_13, 3 bits wide
  assign and_14_out = {Read_Reg_1[1], 1'b1, Read_Reg_1[1]} & {3{and_8_out[2]}};  // And and_14, 3 bits wide
  assign and_15_out = {Read_Reg_1[1], 2'b11} & {3{and_9_out[2]}};  // And and_15, 3 bits wide
  assign and_16_out = {1'b1, {2{Read_Reg_1[1]}}} & {3{and_10_out[2]}};  // And and_16, 3 bits wide
  assign and_17_out = {1'b1, Read_Reg_1[1], 1'b1} & {3{and_11_out[2]}};  // And and_17, 3 bits wide
  assign ALU_Op = and_12_out ^ and_13_out ^ and_14_out ^ and_15_out ^ and_16_out ^ and_17_out;  // XOr xor_1, 3 bits wide

  assign Fetch_Enable = 1'b1;
  assign Increment = 1'b1;
  assign Read_Reg_2 = {Read_Reg_1[1], 1'b1};
  assign Write_Reg = {2{Read_Reg_1[1]}};
  // also tied to GND on the sheet: Read_Reg_1[1]
endmodule
