// Digital circuit memory_Module.dig as structural Verilog
module memory_Module (
  input  [3:0] Clear,
  input  Clock,
  input  [3:0] Data,
  input  [1:0] SP,
  input  [3:0] A,
  output [3:0] Output
);

  wire [3:0] Register_0_p3, Register_1_p3, Register_2_p3, Register_3_p3, Register_4_p3, Register_5_p3,
       Register_6_p3, Register_7_p3, Register_8_p3, Register_9_p3, Register_10_p3, Register_11_p3,
       Register_12_p3, Register_13_p3, Register_14_p3, Register_15_p3;

  Demultiplexer #(.Selector_Bits(4), .Bits(2)) demultiplexer_1 (
    .sel(A), .in(SP));  // open: out_0, out_1, out_2, out_3, out_4, out_5, out_6, out_7, out_8, out_9, out_10, out_11, out_12, out_13, out_14, out_15
  // _4_bit_register Register_0: pin names not known; wires that end beside it: Clock, Clear, Register_0_p3
  // _4_bit_register Register_1: pin names not known; wires that end beside it: Clock, Clear, Register_1_p3
  // _4_bit_register Register_2: pin names not known; wires that end beside it: Clock, Clear, Register_2_p3
  // _4_bit_register Register_3: pin names not known; wires that end beside it: Clock, Clear, Register_3_p3
  // _4_bit_register Register_4: pin names not known; wires that end beside it: Clock, Clear, Register_4_p3
  // _4_bit_register Register_5: pin names not known; wires that end beside it: Clock, Clear, Register_5_p3
  // _4_bit_register Register_6: pin names not known; wires that end beside it: Clock, Clear, Register_6_p3
  // _4_bit_register Register_7: pin names not known; wires that end beside it: Clock, Clear, Register_7_p3
  // _4_bit_register Register_8: pin names not known; wires that end beside it: Clock, Clear, Register_8_p3
  // _4_bit_register Register_9: pin names not known; wires that end beside it: Clock, Clear, Register_9_p3
  // _4_bit_register Register_10: pin names not known; wires that end beside it: Clock, Clear, Register_10_p3
  // _4_bit_register Register_11: pin names not known; wires that end beside it: Clock, Clear, Register_11_p3
  // _4_bit_register Register_12: pin names not known; wires that end beside it: Clock, Clear, Register_12_p3
  // _4_bit_register Register_13: pin names not known; wires that end beside it: Clock, Clear, Register_13_p3
  // _4_bit_register Register_14: pin names not known; wires that end beside it: Clock, Clear, Register_14_p3
  // _4_bit_register Register_15: pin names not known; wires that end beside it: Clock, Clear, Register_15_p3
  Multiplexer #(.Bits(4), .Selector_Bits(4)) multiplexer_1 (
    .in_0(Register_0_p3), .in_1(Register_1_p3), .in_2(Register_2_p3), .in_3(Register_3_p3),
    .in_4(Register_4_p3), .in_5(Register_5_p3), .in_6(Register_6_p3), .in_7(Register_7_p3),
    .in_8(Register_8_p3), .in_9(Register_9_p3), .in_10(Register_10_p3), .in_11(Register_11_p3),
    .in_12(Register_12_p3), .in_13(Register_13_p3), .in_14(Register_14_p3), .in_15(Register_15_p3),
    .out(Output));  // open: sel
  // Pins of 1 and 4 bits meet at A
endmodule
